// Logisim project abundio.circ as structural Verilog: 1 circuit, main circuit main
module main (
  input  pre,
  input  clr
);

  wire clk_out, J0_out, J1_out, J2_out, J3_out, K0_out, n7_segment_display_driver_1_p5,
       n7_segment_display_driver_1_p6, n7_segment_display_driver_1_p7, n7_segment_display_driver_1_p8,
       n7_segment_display_driver_1_p9, n7_segment_display_driver_1_p10, n7_segment_display_driver_1_p11,
       Q0_q, Q0_Q3_out, Q1_q, Q1_qn, Q2_prime_Q1_prime_out, Q2_q, Q2_qn, Q3_q, Q3_qn;

  Clock clk (.out(clk_out));
  J_K_Flip_Flop Q0 (.J(J0_out), .clk(clk_out), .K(K0_out), .Q(Q0_q));  // open: Qn, preset, en, reset
  and J0 (J0_out, Q1_qn, Q2_qn, Q3_qn);
  J_K_Flip_Flop Q1 (.J(J1_out), .clk(clk_out), .K(1'b1), .Q(Q1_q), .Qn(Q1_qn), .preset(pre), .reset(clr));  // open: en
  and J1 (J1_out, Q2_prime_Q1_prime_out, Q0_Q3_out);
  or Q0_Q3 (Q0_Q3_out, Q0_q, Q3_q);
  and Q2_prime_Q1_prime (Q2_prime_Q1_prime_out, Q1_qn, Q2_qn);
  and J3 (J3_out, Q0_q, Q1_q);
  J_K_Flip_Flop Q2 (.J(J2_out), .clk(clk_out), .K(1'b1), .Q(Q2_q), .Qn(Q2_qn));  // open: preset, en, reset
  and K0 (K0_out, Q2_q, Q3_qn);
  J_K_Flip_Flop Q3 (.J(J3_out), .clk(clk_out), .K(1'b1), .Q(Q3_q), .Qn(Q3_qn));  // open: preset, en, reset
  and J2 (J2_out, Q0_q, Q3_q);
  _7_Segment_Display u_7_segment_display_1 (
    .g(n7_segment_display_driver_1_p11), .f(n7_segment_display_driver_1_p10),
    .a(n7_segment_display_driver_1_p5), .b(n7_segment_display_driver_1_p6),
    .e(n7_segment_display_driver_1_p9), .d(n7_segment_display_driver_1_p8), .c(n7_segment_display_driver_1_p7));  // open: dp
  // _7_segment_display_driver 7_segment_display_driver_1: pin names not known; wires that end beside it: Q3_q, Q2_q, Q1_q, Q0_q, n7_segment_display_driver_1_p5, n7_segment_display_driver_1_p6, n7_segment_display_driver_1_p7, n7_segment_display_driver_1_p8, n7_segment_display_driver_1_p9, n7_segment_display_driver_1_p10, n7_segment_display_driver_1_p11

  // Notes on the sheet:
  //   Stephanie Abundio
  //   Final Project 
  //   July 3 2025
  //   JK Flip Flop - 7 seg display
endmodule
